// Logisim project Lab 04.circ as structural Verilog: 4 circuits, main circuit main
module main (
  input  W,
  input  X,
  input  Y,
  input  Z,
  output B,
  output out_6,
  output out_7,
  output D
);

  wire ic7404_1_out_10, ic7404_1_out_11, ic7404_1_out_12, ic_7408_1_out_9, ic_7408_1_out_10,
       ic_7408_1_out_11, ic_7408_1_out_12, ic_7408_2_out_9, ic_7408_2_out_11, ic_7408_2_out_12,
       ic_7432_1_out_9, ic_7432_1_out_11;

  ic_7408 ic_7408_1 (
    .in_1(Z), .in_2(ic7404_1_out_10), .in_3(ic7404_1_out_10), .in_4(ic_7408_1_out_11), .in_5(Z), .in_6(X),
    .in_7(Y), .in_8(X), .out_9(ic_7408_1_out_9), .out_10(ic_7408_1_out_10), .out_11(ic_7408_1_out_11),
    .out_12(ic_7408_1_out_12));
  ic7404 ic7404_1 (
    .in_1(Z), .in_4(X), .in_5(Y), .in_6(Z), .out_7(D), .out_10(ic7404_1_out_10), .out_11(ic7404_1_out_11),
    .out_12(ic7404_1_out_12));  // open: in_2, in_3, out_8, out_9
  ic_7432 ic_7432_1 (
    .in_1(ic_7408_1_out_9), .in_2(ic_7408_1_out_10), .in_3(ic_7432_1_out_9), .in_4(ic_7408_2_out_11),
    .in_5(ic_7408_1_out_12), .in_6(ic_7408_1_out_11), .in_7(ic_7432_1_out_11), .in_8(W),
    .out_9(ic_7432_1_out_9), .out_10(B), .out_11(ic_7432_1_out_11), .out_12(out_6));
  ic_7408 ic_7408_2 (
    .in_1(Y), .in_2(Z), .in_5(X), .in_6(ic_7408_2_out_12), .in_7(ic7404_1_out_11), .in_8(ic7404_1_out_12),
    .out_9(ic_7408_2_out_9), .out_11(ic_7408_2_out_11), .out_12(ic_7408_2_out_12));  // open: in_3, in_4, out_10
  ic_7432 ic_7432_2 (
    .in_7(ic_7408_2_out_9), .in_8(ic_7408_2_out_12), .out_12(out_7));  // open: in_1, in_2, in_3, in_4, in_5, in_6, out_9, out_10, out_11

  // Notes on the sheet:
  //   XZ
  //   XY
  //   X'
  //   Y'
  //   Z'
  //   X'Y
  //   X'Z
  //   XZ+XY
  //   A
  //   XZ'Y'
  //   Z'Y'
  //   Z'
  //   X'Z+X'Y
  //   YZ
  //   C
endmodule

module ic7404 (
  input  in_1,
  input  in_2,
  input  in_3,
  input  in_4,
  input  in_5,
  input  in_6,
  output out_7,
  output out_8,
  output out_9,
  output out_10,
  output out_11,
  output out_12
);

  not not_1 (out_7, in_1);
  not not_2 (out_8, in_2);
  not not_3 (out_9, in_3);
  not not_4 (out_10, in_4);
  not not_5 (out_11, in_5);
  not not_6 (out_12, in_6);
endmodule

module ic_7408 (
  input  in_1,
  input  in_2,
  input  in_3,
  input  in_4,
  input  in_5,
  input  in_6,
  input  in_7,
  input  in_8,
  output out_9,
  output out_10,
  output out_11,
  output out_12
);

  and and_1 (out_9, in_1, in_2);
  and and_2 (out_10, in_3, in_4);
  and and_3 (out_11, in_5, in_6);
  and and_4 (out_12, in_7, in_8);
endmodule

module ic_7432 (
  input  in_1,
  input  in_2,
  input  in_3,
  input  in_4,
  input  in_5,
  input  in_6,
  input  in_7,
  input  in_8,
  output out_9,
  output out_10,
  output out_11,
  output out_12
);

  or or_1 (out_9, in_1, in_2);
  or or_2 (out_10, in_3, in_4);
  or or_3 (out_11, in_5, in_6);
  or or_4 (out_12, in_7, in_8);
endmodule
