// Logisim project lab 5.circ as structural Verilog: 3 circuits, main circuit main
module main (
  input  A3,
  input  A2,
  input  A1,
  input  A0,
  input  B3,
  input  B2,
  input  B1,
  input  B0,
  input  C_in,
  output [3:0] out_10,
  output C_out
);

  wire ic_7486_1_out_9, ic_7486_1_out_10, ic_7486_1_out_11, ic_7486_1_out_12;

  ic_7486 ic_7486_1 (
    .in_1(C_in), .in_2(B3), .in_3(C_in), .in_4(B2), .in_5(B0), .in_6(C_in), .in_7(B1), .in_8(C_in),
    .out_9(ic_7486_1_out_9), .out_10(ic_7486_1_out_10), .out_11(ic_7486_1_out_11), .out_12(ic_7486_1_out_12));
  ic_74283 ic_74283_1 (
    .in_1(C_in), .A0(A0), .B0(ic_7486_1_out_11), .A1(A1), .B1(ic_7486_1_out_12), .A2(A2),
    .B2(ic_7486_1_out_10), .A3(A3), .B3(ic_7486_1_out_9), .out_10(out_10), .out_11(C_out));
endmodule

module ic_74283 (
  input  in_1,
  input  A0,
  input  B0,
  input  A1,
  input  B1,
  input  A2,
  input  B2,
  input  A3,
  input  B3,
  output [3:0] out_10,
  output out_11
);

  wire adder_1_cout, adder_2_cout, adder_3_cout, xor_1_out, xor_2_out, xor_3_out, xor_4_out;

  xor xor_1 (xor_1_out, B0, in_1);
  xor xor_2 (xor_2_out, B1, in_1);
  xor xor_3 (xor_3_out, B2, in_1);
  xor xor_4 (xor_4_out, B3, in_1);
  Adder #(.width(1)) adder_1 (.a(A0), .b(xor_1_out), .out(out_10[0]), .cin(in_1), .cout(adder_1_cout));
  Adder #(.width(1)) adder_2 (.a(A1), .b(xor_2_out), .out(out_10[1]), .cin(adder_1_cout), .cout(adder_2_cout));
  Adder #(.width(1)) adder_3 (.a(A2), .b(xor_3_out), .out(out_10[2]), .cin(adder_2_cout), .cout(adder_3_cout));
  Adder #(.width(1)) adder_4 (.a(A3), .b(xor_4_out), .out(out_10[3]), .cin(adder_3_cout), .cout(out_11));
endmodule

module ic_7486 (
  input  in_1,
  input  in_2,
  input  in_3,
  input  in_4,
  input  in_5,
  input  in_6,
  input  in_7,
  input  in_8,
  output out_9,
  output out_10,
  output out_11,
  output out_12
);

  xor xor_1 (out_9, in_1, in_2);
  xor xor_2 (out_10, in_3, in_4);
  xor xor_3 (out_11, in_5, in_6);
  xor xor_4 (out_12, in_7, in_8);
endmodule
