// Logisim project Decoder.circ as structural Verilog: 1 circuit, main circuit main
module main (
  input  in_1,
  input  [2:0] in_2
);

  wire not_1_out;

  not not_1 (not_1_out, in_1);
  Decoder #(.select(3)) decoder_1 (.sel(in_2), .en(not_1_out));  // open: out0, out1, out2, out3, out4, out5, out6, out7
endmodule
