// Logisim project avtive low decoder.circ as structural Verilog: 1 circuit, main circuit main
module main (
  input  [2:0] in_1,
  output [7:0] out_2
);

  wire decoder_1_out0, decoder_1_out1, decoder_1_out2, decoder_1_out3, decoder_1_out4, decoder_1_out5,
       decoder_1_out6, decoder_1_out7;

  Decoder #(.select(3), .enable("false")) decoder_1 (
    .out0(decoder_1_out0), .out1(decoder_1_out1), .out2(decoder_1_out2), .out3(decoder_1_out3),
    .out4(decoder_1_out4), .out5(decoder_1_out5), .out6(decoder_1_out6), .out7(decoder_1_out7), .sel(in_1));
  not not_1 (out_2[0], decoder_1_out0);
  not not_2 (out_2[6], decoder_1_out6);
  not not_3 (out_2[7], decoder_1_out7);
  not not_4 (out_2[1], decoder_1_out1);
  not not_5 (out_2[3], decoder_1_out3);
  not not_6 (out_2[4], decoder_1_out4);
  not not_7 (out_2[5], decoder_1_out5);
  not not_8 (out_2[2], decoder_1_out2);
endmodule
