// Logisim project Week2.circ as structural Verilog
module ic7400 (
  input  A,
  input  A_2,
  input  B,
  input  A_3,
  input  B_2,
  output A_prime,
  output out_7,
  output out_8
);

  wire nand_2_out, nand_3_out, nand_4_out;

  nand nand_1 (A_prime, A, A);
  nand nand_2 (nand_2_out, A_2, B);
  nand nand_3 (nand_3_out, A_3, A_3);
  nand nand_4 (nand_4_out, B_2, B_2);
  nand nand_5 (out_8, nand_3_out, nand_4_out);
  nand nand_6 (out_7, nand_2_out, nand_2_out);

  // Notes on the sheet:
  //   (AB)'
  //   (A+B)
  //   AB
endmodule

module ic7402 (
  input  A,
  input  A_2,
  input  B,
  input  A_3,
  input  B_2,
  output A_prime,
  output out_7,
  output A_B
);

  wire nor_2_out, nor_3_out, nor_4_out;

  nor nor_1 (A_prime, A, A);
  nor nor_2 (nor_2_out, A_2, A_2);
  nor nor_3 (nor_3_out, B, B);
  nor nor_4 (nor_4_out, A_3, B_2);
  nor nor_5 (A_B, nor_4_out, nor_4_out);
  nor nor_6 (out_7, nor_2_out, nor_3_out);

  // Notes on the sheet:
  //   AB
endmodule
