// Logisim project task 3 using nor.circ as structural Verilog: 2 circuits, main circuit main
module main (
  input  A,
  input  B,
  input  C
);

  ic7402 ic7402_1 ();  // open: in_1, in_2, in_3, in_4, in_5, in_6, in_7, in_8, out_9, out_10, out_11, out_12
  ic7402 ic7402_2 (.in_5(B), .in_6(B));  // open: in_1, in_2, in_3, in_4, in_7, in_8, out_9, out_10, out_11, out_12
endmodule

module ic7402 (
  input  in_1,
  input  in_2,
  input  in_3,
  input  in_4,
  input  in_5,
  input  in_6,
  input  in_7,
  input  in_8,
  output out_9,
  output out_10,
  output out_11,
  output out_12
);

  nor nor_1 (out_9, in_1, in_2);
  nor nor_2 (out_10, in_3, in_4);
  nor nor_3 (out_11, in_5, in_6);
  nor nor_4 (out_12, in_7, in_8);
endmodule
