// Logisim project task 3.circ as structural Verilog: 2 circuits, main circuit main
module main (
  input  A,
  input  B,
  input  C,
  output out_4
);

  wire ic7400_1_out_9, ic7400_1_out_10, ic7400_1_out_11, ic7400_1_out_12, ic7400_2_out_12, ic7400_3_out_11,
       ic7400_3_out_12;

  ic7400 ic7400_1 (
    .in_1(ic7400_2_out_12), .in_2(B), .in_3(ic7400_1_out_9), .in_4(ic7400_1_out_9), .out_9(ic7400_1_out_9),
    .out_10(ic7400_1_out_10), .in_5(ic7400_1_out_12), .out_11(ic7400_1_out_11), .in_6(ic7400_1_out_12),
    .in_7(C), .out_12(ic7400_1_out_12), .in_8(A));
  ic7400 ic7400_2 (
    .in_7(C), .out_12(ic7400_2_out_12), .in_8(C));  // open: in_1, in_2, in_3, in_4, out_9, out_10, in_5, out_11, in_6
  ic7400 ic7400_3 (
    .in_3(ic7400_3_out_11), .in_4(ic7400_3_out_12), .out_10(out_4), .in_5(ic7400_1_out_11),
    .out_11(ic7400_3_out_11), .in_6(ic7400_1_out_11), .in_7(ic7400_1_out_10), .out_12(ic7400_3_out_12),
    .in_8(ic7400_1_out_10));  // open: in_1, in_2, out_9
endmodule

module ic7400 (
  input  in_1,
  input  in_2,
  input  in_3,
  input  in_4,
  input  in_5,
  input  in_6,
  input  in_7,
  input  in_8,
  output out_9,
  output out_10,
  output out_11,
  output out_12
);

  nand nand_1 (out_9, in_1, in_2);
  nand nand_2 (out_10, in_3, in_4);
  nand nand_3 (out_11, in_5, in_6);
  nand nand_4 (out_12, in_7, in_8);
endmodule
