// Logisim project 1st Cononical form.circ as structural Verilog: 4 circuits, main circuit main
module main (
  input  A,
  input  B,
  input  C,
  output out_4
);

  wire ic7404_1_out_10, ic7404_1_out_11, ic7404_1_out_12, ic7411_1_out_10, ic7411_1_out_11, ic7411_1_out_12;

  ic7411 ic7411_1 (
    .A(ic7404_1_out_12), .B(ic7404_1_out_11), .C(C), .in_4(A), .in_5(B), .in_6(ic7404_1_out_10),
    .in_7(ic7404_1_out_10), .in_8(C), .in_9(ic7404_1_out_12), .out_10(ic7411_1_out_10),
    .out_11(ic7411_1_out_11), .out_12(ic7411_1_out_12));
  ic7404 ic7404_1 (
    .in_4(C), .in_5(B), .in_6(A), .out_10(ic7404_1_out_10), .out_11(ic7404_1_out_11), .out_12(ic7404_1_out_12));  // open: in_1, in_2, in_3, out_7, out_8, out_9
  ic4075 ic4075_1 (
    .in_7(ic7411_1_out_10), .in_8(ic7411_1_out_12), .in_9(ic7411_1_out_11), .out_12(out_4));  // open: in_1, in_2, in_3, in_4, in_5, in_6, out_10, out_11

  // Notes on the sheet:
  //   A'BC'
  //   A'B'C
  //   A'
  //   C'
  //   B'
  //   ABC'
endmodule

module ic7411 (
  input  A,
  input  B,
  input  C,
  input  in_4,
  input  in_5,
  input  in_6,
  input  in_7,
  input  in_8,
  input  in_9,
  output out_10,
  output out_11,
  output out_12
);

  and and_1 (out_10, A, B, C);
  and and_2 (out_11, in_4, in_5, in_6);
  and and_3 (out_12, in_7, in_8, in_9);
endmodule

module ic4075 (
  input  in_1,
  input  in_2,
  input  in_3,
  input  in_4,
  input  in_5,
  input  in_6,
  input  in_7,
  input  in_8,
  input  in_9,
  output out_10,
  output out_11,
  output out_12
);

  or or_1 (out_10, in_1, in_2, in_3);
  or or_2 (out_11, in_4, in_5, in_6);
  or or_3 (out_12, in_7, in_8, in_9);
endmodule

module ic7404 (
  input  in_1,
  input  in_2,
  input  in_3,
  input  in_4,
  input  in_5,
  input  in_6,
  output out_7,
  output out_8,
  output out_9,
  output out_10,
  output out_11,
  output out_12
);

  not not_1 (out_7, in_1);
  not not_2 (out_8, in_2);
  not not_3 (out_9, in_3);
  not not_4 (out_10, in_4);
  not not_5 (out_11, in_5);
  not not_6 (out_12, in_6);
endmodule
