// Logisim project lab 7.circ as structural Verilog: 1 circuit, main circuit main
module main (
  input  A,
  input  A_2,
  input  B,
  input  C,
  input  C_2,
  input  B_2,
  input  D,
  input  D_2,
  input  B_3,
  input  A_3,
  input  C_3,
  input  B_4,
  input  D_3,
  input  C_4,
  input  D_4,
  input  B_5,
  input  C_5,
  input  D_5,
  input  A_4,
  input  B_6,
  input  D_6,
  input  C_6,
  input  A_5,
  input  C_7,
  input  B_7,
  input  D_7
);

  wire and_1_out, and_2_out, and_3_out, and_4_out, and_5_out, and_6_out, and_7_out, and_8_out, and_9_out,
       and_10_out, and_11_out, and_12_out, and_13_out, and_14_out, and_15_out, and_16_out, not_1_out,
       not_2_out, not_3_out, not_4_out, not_5_out, not_6_out, not_7_out, not_8_out, not_9_out, not_10_out,
       not_11_out, not_12_out, not_13_out, not_14_out, not_15_out, not_16_out, or_1_out, or_2_out, or_3_out,
       or_4_out, or_5_out, or_6_out, or_7_out;

  not not_1 (not_1_out, B_7);
  not not_2 (not_2_out, D_4);
  not not_3 (not_3_out, D_7);
  not not_4 (not_4_out, C_7);
  not not_5 (not_5_out, B);
  not not_6 (not_6_out, D);
  not not_7 (not_7_out, C_2);
  not not_8 (not_8_out, C_4);
  and and_1 (and_1_out, not_3_out, C_7);
  and and_2 (and_2_out, not_1_out, not_3_out);
  and and_3 (and_3_out, not_4_out, B_7, D_7);
  and and_4 (and_4_out, not_1_out, C_7);
  and and_5 (and_5_out, not_5_out, C_2);
  and and_6 (and_6_out, C_2, not_6_out);
  and and_7 (and_7_out, not_7_out, B);
  and and_8 (and_8_out, B_4, not_8_out);
  and and_9 (and_9_out, not_8_out, not_2_out);
  and and_10 (and_10_out, not_2_out, B_4);
  or or_1 (or_1_out, A_5, and_1_out, and_2_out, and_3_out, and_4_out);
  or or_2 (or_2_out, A, and_5_out, and_6_out, and_7_out);
  or or_3 (or_3_out, A_3, and_8_out, and_9_out, and_10_out);
  _7_Segment_Display u_7_segment_display_1 (
    .g(or_2_out), .f(or_3_out), .a(or_6_out), .b(or_7_out), .e(or_4_out), .d(or_1_out), .c(or_5_out));  // open: dp
  or or_4 (or_4_out, and_13_out, and_11_out);
  not not_9 (not_9_out, D_2);
  and and_11 (and_11_out, not_16_out, C_6);
  not not_10 (not_10_out, B_2);
  and and_12 (and_12_out, B_2, D_2);
  not not_11 (not_11_out, B_3);
  not not_12 (not_12_out, D_3);
  not not_13 (not_13_out, C_3);
  not not_14 (not_14_out, C_5);
  and and_13 (and_13_out, not_15_out, not_16_out);
  and and_14 (and_14_out, not_12_out, not_13_out);
  and and_15 (and_15_out, C_3, D_3);
  not not_15 (not_15_out, B_6);
  not not_16 (not_16_out, D_6);
  and and_16 (and_16_out, not_10_out, not_9_out);
  or or_5 (or_5_out, B_5, not_14_out, D_5);
  or or_6 (or_6_out, A_2, C, and_12_out, and_16_out);
  or or_7 (or_7_out, not_11_out, and_14_out, and_15_out);

  // Notes on the sheet:
  //   g=B'C+CD'+BC'+A
  //   f= A+C'D'+BC'+BD'
  //   d=A+B'D'+CD'+BC'D+B'C
  //   CD'
  //   B'D'
  //   BC'D
  //   B'C
  //   CD'
  //   BC'
  //   BC'
  //   C'D'
  //   BD'
  //   B'C
  //   b=B'+CD+C'D'
  //   a=A+C+BD+B'D'
  //   c=B+C'+D
  //   B'D'
  //   D'C
  //   e=B'D'+CD'
endmodule
